# Fritzing sketch ReleSoloSketch (saved by Fritzing 0.9.3b)
breadboards: 1

parts:
  U1 = RELAY [package=relay-g5q]
  Componente1 = Arduino Uno (Rev3) - ICSP
  J1 = Power Jack [package=power_jack_smd]

nets:
  N1: U1.COIL2, Componente1.D7
  N2: U1.NO, Componente1.GND
  N3: U1.COIL1, J1.GNDBREAK

notes:
  Camara ip o Sirena
