# Fritzing sketch releSketch (saved by Fritzing 0.9.3b)
breadboards: 1

parts:
  U1 = RELAY [package=relay-jzc]
  U2 = RELAY [package=relay-jzc]
  Componente1 = Arduino Uno (Rev3) - ICSP
  J1 = Power Jack [package=power_jack_smd]  # not connected

nets:
  N1: U1.COIL2, U2.COIL2, Componente1.5V
  N2: U1.NC, U2.NC, Componente1.GND
  N3: U1.NO, Componente1.D2
  N4: U2.NO, Componente1.D4

notes:
  Fuente de 12v
  Sirena
  Camara IP
